# Fritzing sketch Circuit Diagram (saved by Fritzing 0.9.3b)

parts:
  Part1 = Arduino Uno (Rev3) - ICSP
  Part2 = Bluetooth HC-05 Macho
  LED1 = smd LED [color="Red (633nm)" package="1206 [SMD]"]
  L298N1 = L298N DC motor driver
  VCC1 = Battery
  M4 = DC Motor  # not connected
  M5 = DC Motor  # not connected
  M6 = DC Motor  # not connected
  M7 = DC Motor  # not connected

nets:
  N1: Part1.ICSP_MISO, Part1.D12/MISO, L298N1.IN2
  N2: Part1.D9_PWM, LED1.cathode
  N3: Part1.D10_PWM/SS, L298N1.IN4
  N4: Part1.D11_PWM/MOSI, L298N1.IN3
  N5: Part1.D13/SCK, L298N1.IN1
  N6: Part1.D0/RX, Part2.TXD
  N7: Part1.D1/TX, Part2.RXD
  N8: Part1.3V3, LED1.anode
  5V: Part1.5V, Part2.VCC
  GND: Part1.GND, Part2.GND, L298N1.GND, VCC1.-
  VIN: Part1.VIN, L298N1.5V
  N9: L298N1.12V, VCC1.+

custom parts:
  L298N DC motor driver: 2x DC motor driver with 78M05 positive voltage regulator (7..35 V) L298N: max 46 V, 2 A Set 5 V Enable jumper to enable 5 V regultor (needed for the L298N) and +5 V output at screw terminal or supply external +5 V at screw terminal Set ENA and/or ENB to +5 V to enable motor permanently or supply ENA and/or ENB with PWM signal IN1 and IN2 set rotation directory for motor A (OUT1/OUT2) IN2 and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
  Battery: Your standard 2x 18650 battery pack (7,4 Volts)
